# Fritzing sketch ControlPaty (saved by Fritzing 1.0.1rc)
breadboards: 1

parts:
  Mod1 = Amica NodeMCU DEVKIT 1.0
  S1 = Pushbutton [package="[THT]"]
  LED1 = LED - 5mm [color="Red (635nm)" current=0.030A package="5 mm [THT]"]
  R1 = Resistor [tolerance=±5% power=0.25W resistance=330 package=THT]
  R2 = Resistor [tolerance=±5% power=0.25W resistance=10k package=THT]
  OLED1 = OLED 128x64 I2C Monochrome Display
  S2 = Pushbutton [package="[THT]"]
  LED2 = LED - 5mm [color="Red (635nm)" current=0.030A package="5 mm [THT]"]
  R3 = Resistor [tolerance=±5% power=0.25W resistance=330 package=THT]
  R4 = Resistor [tolerance=±5% power=0.25W resistance=10k package=THT]
  LED3 = LED - 5mm [color="Red (635nm)" current=0.030A package="5 mm [THT]"]
  R5 = Resistor [tolerance=±5% power=0.25W resistance=330 package=THT]

nets:
  N1: Mod1.pin1, Mod1.pin2, Mod1.pin_9, Mod1.pin_10, Mod1.pin_25, Mod1.pin_26, Mod1.pin_29, S1.Pin_1, S1.Pin_2, LED1.anode, R2.Pin_0, OLED1.GND, S2.Pin_1, S2.Pin_2, LED2.anode, R4.Pin_0, LED3.anode
  N2: Mod1.pin5, R5.Pin_0
  N3: Mod1.pin6, S1.Pin_3, S1.Pin_4, R2.Pin_1
  N4: Mod1.pin7, S2.Pin_3, S2.Pin_4, R4.Pin_1
  N5: Mod1.pin8, R1.Pin_0
  N6: Mod1.pin_12, R3.Pin_0
  N7: Mod1.pin_13, OLED1.SDA
  N8: Mod1.pin_14, OLED1.SCK
  N9: Mod1.pin_30, OLED1.VDD
  N10: LED1.cathode, R1.Pin_1
  N11: LED2.cathode, R3.Pin_1
  N12: LED3.cathode, R5.Pin_1
